# Fritzing sketch CPE301_Midter1_IOTProject (saved by Fritzing 0.9.3b)
breadboards: 1

parts:
  U1 = atmega328 [package=dip]
  T1 = LM34 Temperature Sensor [package="TO92 [THT]"]
  U3 = ESP8266 WiFi Module [part_number=ESP8266]
  V1 = DC Power [voltage=3.3V]
  R1 = Resistor [tolerance=±5% resistance=2.2k package=THT]
  R2 = Resistor [tolerance=±5% resistance=4.7k package=THT]
  R3 = Resistor [tolerance=±5% resistance=3.3k package=THT]
  Push_Button = Pushbutton [package="[THT]"]

nets:
  N1: U1.RESET, Push_Button.Pin_3
  N2: U1.D0_(RX), U3.TXD
  N3: U1.D1_(TX), R1.Pin_0
  N4: U1.VCC, T1.+Vs
  N5: U1.AVCC, U3.VCC, U3.CH_PD, V1.V+, R3.Pin_1
  GND: U1.GND, T1.GND, U3.GND, V1.V-, R2.Pin_1, Push_Button.Pin_1
  N6: U1.A0, T1.Vout
  N7: U3.RXD, R1.Pin_1, R2.Pin_0
  N8: U3.REST, R3.Pin_0
